# Fritzing sketch example_sketch (saved by Fritzing 0.9.3b)

parts:
  WeMos_D1_Mini1 = WeMos D1 Mini
  8_Channel_Relay1 = 8 Channel Power Relay
  U1 = LIPO-1000mAh [package=lipo-1000]
  LED1 = LED - 3mm [color="Red (633nm)" package="3 mm [THT]"]
  LED3 = LED - 3mm [color="Red (633nm)" package="3 mm [THT]"]
  LED4 = LED - 3mm [color="Red (633nm)" package="3 mm [THT]"]
  LED5 = LED - 3mm [color="Red (633nm)" package="3 mm [THT]"]
  J2 = Camdenboss CTB0158-4 [part_number=CTB0158-4 package=THT]
  J3 = Camdenboss CTB0158-4 [part_number=CTB0158-4 package=THT]

nets:
  5V: WeMos_D1_Mini1.5V, 8_Channel_Relay1.VCC
  N1: WeMos_D1_Mini1.D1, 8_Channel_Relay1.IN1
  N2: WeMos_D1_Mini1.D2, 8_Channel_Relay1.IN2
  N3: WeMos_D1_Mini1.D3, 8_Channel_Relay1.IN3
  N4: WeMos_D1_Mini1.D4, 8_Channel_Relay1.IN4
  N5: WeMos_D1_Mini1.D5, 8_Channel_Relay1.IN5
  N6: WeMos_D1_Mini1.D6, 8_Channel_Relay1.IN6
  N7: WeMos_D1_Mini1.D7, 8_Channel_Relay1.IN7
  N8: WeMos_D1_Mini1.D8, 8_Channel_Relay1.IN8
  N9: WeMos_D1_Mini1.G, 8_Channel_Relay1.GND
  N10: 8_Channel_Relay1.COM#22, U1.-, J2.terminal_1
  N11: 8_Channel_Relay1.NO#23, LED1.anode
  N12: 8_Channel_Relay1.COM#25, J2.terminal_2
  N13: 8_Channel_Relay1.NO#26, LED5.anode
  N14: 8_Channel_Relay1.COM#28, J2.terminal_3
  N15: 8_Channel_Relay1.NO#29, LED3.anode
  N16: 8_Channel_Relay1.COM#31, J2.terminal_4
  N17: 8_Channel_Relay1.NO#32, LED4.anode
  N18: U1.+, LED1.cathode, J3.terminal_1
  N19: LED3.cathode, J3.terminal_3
  N20: LED4.cathode, J3.terminal_4
  N21: LED5.cathode, J3.terminal_2

notes:
  + all connected at terminal
  - all connected at terminal
  I did only 4 because I'm lazy
  Most likely a regulator would be needed to supply the correct voltage and current to the ignition devices

custom parts:
  8 Channel Power Relay: An 8 channel power relay. The module operates at 5V.
